// Logisim project 4bitCraaph.circ as structural Verilog: 1 circuit, main circuit main
module main (
);

  wire AB, ALU_B, BB, CLK, EN_A, EN_B, EN_M, JMP, LSB, MB, MSB, OPB;
  wire [1:0] ALU_S;
  wire [3:0] A, adder_1_out, B, DBUS, MAR_q, MEM, multiplexer_1_out, nand_1_out, nor_1_out, OPERAN,
       register_1_q, register_2_q, rom_1_data, subtractor_1_out;
  wire [7:0] controlled_buffer_1_out;
  wire [10:0] pla_1_out;

  Clock clock_1 (.out(CLK));
  Register #(.trigger("falling"), .width(4)) register_1 (.D(DBUS), .en(LSB), .Q(register_1_q), .clk(CLK));  // open: clr
  Register #(.trigger("falling"), .width(4)) register_2 (.D(DBUS), .en(MSB), .Q(register_2_q), .clk(CLK));  // open: clr
  assign controlled_buffer_1_out = JMP ? {register_2_q, register_1_q} : 8'bz;  // Controlled_Buffer controlled_buffer_1
  Adder #(.width(4)) adder_1 (.a(A), .b(B), .out(adder_1_out));  // open: cin, cout
  Subtractor #(.width(4)) subtractor_1 (.a(A), .b(B), .out(subtractor_1_out));  // open: bin, bout
  assign nand_1_out = ~(A & B);  // NAND_Gate nand_1, 4 bits wide
  assign nor_1_out = ~(A | B);  // NOR_Gate nor_1, 4 bits wide
  Comparator #(.mode("unsigned"), .width(4)) comparator_1 (.a(A), .b(B));  // open: gt, eq, lt
  ROM rom_1 (.addr(controlled_buffer_1_out), .data({OPERAN, rom_1_data}));
  Multiplexer #(.select(2), .width(4)) multiplexer_1 (
    .in0(adder_1_out), .in1(subtractor_1_out), .in2(nand_1_out), .in3(nor_1_out), .out(multiplexer_1_out),
    .sel(ALU_S));
  assign DBUS = ALU_B ? multiplexer_1_out : 4'bz;  // Controlled_Buffer controlled_buffer_2
  Register #(.width(4)) MAR (.D(DBUS), .en(EN_M), .Q(MAR_q), .clk(CLK));  // open: clr
  assign DBUS = OPB ? OPERAN : 4'bz;  // Controlled_Buffer controlled_buffer_3
  assign DBUS = AB ? A : 4'bz;  // Controlled_Buffer controlled_buffer_4
  RAM #(.addrWidth(4), .dataWidth(4)) ram_1 (.addr(MAR_q), .dout(MEM));  // open: we, oe, clk, din
  assign DBUS = BB ? B : 4'bz;  // Controlled_Buffer controlled_buffer_5
  assign DBUS = MB ? MEM : 4'bz;  // Controlled_Buffer controlled_buffer_6
  PLA #(.in_width(4), .out_width(11), .\table ("0000 00000000000\n0001 00000000000\n0010 00000000000\n0011 00000000000\n0100 00000000000\n0101 00000000000\n0110 00000000000\n0111 00000000000")) pla_1 (
    .in(rom_1_data), .out(pla_1_out));
  Register #(.width(4)) register_3 (.D(DBUS), .en(EN_A), .Q(A), .clk(CLK));  // open: clr
  Register #(.width(4)) register_4 (.D(DBUS), .en(EN_B), .Q(B), .clk(CLK));  // open: clr
endmodule
