// Logisim project crapph.circ as structural Verilog: 4 circuits, main circuit main
module main (
);

  wire clock_1_out, decoder_1_out0, decoder_1_out1, decoder_1_out2, decoder_1_out3, decoder_1_out4,
       decoder_1_out5, decoder_1_out6, decoder_1_out7, decoder_1_out14, decoder_1_out15, not_1_out,
       not_2_out, or_1_out, or_2_out, or_3_out, t_ff_1_q;
  wire [7:0] adder_1_out, controlled_buffer_1_out, counter_1_q, register_1_q, register_2_q, register_3_q;
  wire [11:0] rom_1_data;

  T_Flip_Flop t_ff_1 (.clk(clock_1_out), .T(decoder_1_out14), .Q(t_ff_1_q));  // open: Qn, preset, reset
  not not_1 (not_1_out, t_ff_1_q);
  Clock clock_1 (.out(clock_1_out));
  ROM #(.dataWidth(12)) rom_1 (.addr(counter_1_q), .data(rom_1_data));
  Counter counter_1 (
    .load(decoder_1_out15), .D(controlled_buffer_1_out), .Q(counter_1_q), .up(not_1_out), .clk(clock_1_out));  // open: count, carry, clr
  Decoder #(.select(4)) decoder_1 (
    .out0(decoder_1_out0), .out1(decoder_1_out1), .out2(decoder_1_out2), .out3(decoder_1_out3),
    .out4(decoder_1_out4), .out5(decoder_1_out5), .out6(decoder_1_out6), .out7(decoder_1_out7),
    .out14(decoder_1_out14), .out15(decoder_1_out15), .sel(rom_1_data[11:8]));  // open: out8, out9, out10, out11, out12, out13, en
  assign controlled_buffer_1_out = not_2_out ? rom_1_data[7:0] : 8'bz;  // Controlled_Buffer controlled_buffer_1
  not not_2 (not_2_out, or_1_out);
  or or_1 (or_1_out, decoder_1_out6, decoder_1_out5, decoder_1_out7);
  assign controlled_buffer_1_out = decoder_1_out3 ? register_2_q : 8'bz;  // Controlled_Buffer controlled_buffer_2
  assign controlled_buffer_1_out = decoder_1_out1 ? register_1_q : 8'bz;  // Controlled_Buffer controlled_buffer_3
  or or_2 (or_2_out, decoder_1_out6, decoder_1_out7);
  assign controlled_buffer_1_out = or_2_out ? adder_1_out : 8'bz;  // Controlled_Buffer controlled_buffer_4
  assign controlled_buffer_1_out = decoder_1_out5 ? register_3_q : 8'bz;  // Controlled_Buffer controlled_buffer_5
  Register register_1 (
    .D(controlled_buffer_1_out), .en(decoder_1_out0), .clk(clock_1_out), .Q(register_1_q));  // open: clr
  Register register_2 (
    .D(controlled_buffer_1_out), .en(decoder_1_out2), .clk(clock_1_out), .Q(register_2_q));  // open: clr
  Adder adder_1 (.a(register_2_q), .b(register_1_q), .out(adder_1_out));  // open: cin, cout
  Register register_3 (.D(controlled_buffer_1_out), .en(or_3_out), .clk(clock_1_out), .Q(register_3_q));  // open: clr
  or or_3 (or_3_out, decoder_1_out4, decoder_1_out7);

  // Notes on the sheet:
  //   contents of rom_1 (hex, n*v repeats v):
  //   53 0 201 521 700
endmodule

module test (
);

  wire AB, ALU_B, and_1_out, and_2_out, and_3_out, asel_en, BB, CB, CLK, clock_2_out, ENA, ENB, ENC, ENT,
       input_sel_en, JMP, MAR, MOE, MWE, OPB, TB;
  wire [2:0] register_10_q;
  wire [3:0] register_9_q;
  wire [4:0] STATUS;
  wire [7:0] OPCODE;
  wire [15:0] A, ALU_OUT, B, C, counter_1_q, DBUS, MEM_OUT, OPERAND, register_6_q, testmuxthing_1_out_8,
       testmuxthing_1_out_9, TMP;
  wire [23:0] rom_1_data;
  wire [23:9] DECODER_data;

  Clock clock_1 (.out(CLK));
  assign DBUS = AB ? A : 16'bz;  // Controlled_Buffer controlled_buffer_1
  assign DBUS = BB ? B : 16'bz;  // Controlled_Buffer controlled_buffer_2
  assign DBUS = CB ? C : 16'bz;  // Controlled_Buffer controlled_buffer_3
  assign DBUS = TB ? TMP : 16'bz;  // Controlled_Buffer controlled_buffer_4
  assign DBUS = OPB ? OPERAND : 16'bz;  // Controlled_Buffer controlled_buffer_5
  assign DBUS = ALU_B ? ALU_OUT : 16'bz;  // Controlled_Buffer controlled_buffer_6
  assign DBUS = MOE ? MEM_OUT : 16'bz;  // Controlled_Buffer controlled_buffer_7
  // Probe on OPCODE
  // Probe on OPERAND
  // Probe on DBUS
  // Probe on ALU_OUT
  // Probe on STATUS
  // Probe on A
  Register #(.trigger("falling"), .width(16)) register_1 (.en(1'b1), .clk(CLK));  // open: D, Q, clr
  Register #(.width(16)) register_2 (.D(DBUS), .en(ENA), .Q(A), .clk(CLK));  // open: clr
  Register #(.width(16)) register_3 (.D(DBUS), .en(ENB), .Q(B), .clk(CLK));  // open: clr
  Register #(.width(16)) register_4 (.D(DBUS), .en(ENC), .Q(C), .clk(CLK));  // open: clr
  Register #(.width(16)) register_5 (.D(DBUS), .en(ENT), .Q(TMP), .clk(CLK));  // open: clr
  Register #(.width(16)) register_6 (.D(DBUS), .en(MAR), .Q(register_6_q), .clk(CLK));  // open: clr
  RAM #(.addrWidth(16), .dataWidth(16)) ram_1 (
    .addr(register_6_q), .we(MWE), .oe(1'b1), .clk(CLK), .din(DBUS), .dout(MEM_OUT));
  ROM #(.addrWidth(16), .dataWidth(24)) rom_1 (.addr(counter_1_q), .data(rom_1_data));
  Counter #(.max('hffff), .width(16)) counter_1 (
    .load(JMP), .D(DBUS), .Q(counter_1_q), .up(1'b1), .clk(CLK));  // open: count, carry, clr
  ROM #(.dataWidth(26)) DECODER (
    .addr(OPCODE),
    .data({asel_en, input_sel_en, DECODER_data[23:16], MAR, MOE, MWE, ALU_B, DECODER_data[11:9], ENT, ENC, ENB, ENA, TB, CB, BB, AB, OPB}));
  Register #(.trigger("falling"), .width(16)) register_7 (
    .D(rom_1_data[15:0]), .en(1'b1), .Q(OPERAND), .clk(clock_2_out));  // open: clr
  Clock clock_2 (.out(clock_2_out));
  Register #(.trigger("falling")) register_8 (
    .D(rom_1_data[23:16]), .en(1'b1), .Q(OPCODE), .clk(clock_2_out));  // open: clr
  testMuxThing testmuxthing_1 (
    .in_1(A), .in_2(B), .in_3(C), .in_5(TMP), .in_6(MEM_OUT), .in_7(OPERAND), .in_4(register_9_q),
    .out_8(testmuxthing_1_out_8), .out_9(testmuxthing_1_out_9));
  Register #(.trigger("falling"), .width(4)) register_9 (
    .D(DBUS[3:0]), .en(input_sel_en), .Q(register_9_q), .clk(CLK));  // open: clr
  and and_1 (and_1_out, DECODER_data[16], STATUS[2]);
  and and_2 (and_2_out, DECODER_data[17], STATUS[1]);
  and and_3 (and_3_out, DECODER_data[18], STATUS[0]);
  Register #(.trigger("falling"), .width(3)) register_10 (
    .D(DBUS[2:0]), .en(asel_en), .Q(register_10_q), .clk(CLK));  // open: clr
  alu alu_1 (
    .MUX(register_10_q), .A(testmuxthing_1_out_8), .B(testmuxthing_1_out_9), .in_4(CLK), .Q(ALU_OUT),
    .STATUS(STATUS));
  or or_1 (JMP, and_1_out, and_2_out, and_3_out, DECODER_data[19]);

  // Notes on the sheet:
  //   contents of rom_1 (hex, n*v repeats v):
  //   ff0000 1 240000 60000 30000 300002
  //   contents of DECODER (hex, n*v repeats v):
  //   21 24 28 30 4020 41 42 48 50 4040 81 82 84 90 4080 101 102 104 108 4100 2001 2002 2004 2008 2010
  //   8001 8002 8004 8008 8010 c000 0 3ff1ff1 1020 1040 1080 1100 9000 0 0 1000001 1000002 6*0 80001 10001
  //   20001 40001 30001 60001 201*0 4000
  //   1
  //   2
  //   4
  //   8
  //   1
  //   2
  //   4
  //   8
  //   1
  //   2
  //   4
  //   8
  //   1
  //   2
  //   4
  //   8
  //   1
  //   2
  //   4
  //   8
  //   1
  //   2
  //   4
  //   8
endmodule

module alu (
  input  [15:0] A,
  input  [15:0] B,
  input  [2:0] MUX,
  input  in_4,
  output [15:0] Q,
  output [4:0] STATUS
);

  wire [1:0] C;
  wire [2:0] comparator_1_lt;
  wire [15:0] adder_1_out, and_1_out, divider_1_out, multiplier_1_out, or_1_out, subtractor_1_out, xor_1_out;

  Adder #(.width(16)) adder_1 (.a(A), .b(B), .out(adder_1_out), .cout(C[0]));  // open: cin
  Subtractor #(.width(16)) subtractor_1 (.a(A), .b(B), .out(subtractor_1_out), .bout(C[1]));  // open: bin
  Multiplier #(.width(16)) multiplier_1 (.a(A), .b(B), .out(multiplier_1_out));  // open: cin, cout
  Divider #(.width(16)) divider_1 (.a(A), .b(B), .out(divider_1_out));  // open: upper, rem
  assign or_1_out = A | B;  // OR_Gate or_1, 16 bits wide
  assign and_1_out = A & B;  // AND_Gate and_1, 16 bits wide
  assign xor_1_out = A ^ B;  // XOR_Gate xor_1, 16 bits wide
  Comparator #(.mode("unsigned"), .width(16)) comparator_1 (
    .a(A), .b(B), .gt(comparator_1_lt[2]), .eq(comparator_1_lt[1]), .lt(comparator_1_lt[0]));
  Register #(.trigger("falling"), .width(5)) register_1 (
    .D({C[0], C[1], comparator_1_lt}), .en(1'b1), .clk(in_4), .Q(STATUS));  // open: clr
  Multiplexer #(.select(3), .width(16)) multiplexer_1 (
    .in0(adder_1_out), .in1(subtractor_1_out), .in2(multiplier_1_out), .in3(divider_1_out), .in4(or_1_out),
    .in5(and_1_out), .in6(xor_1_out), .out(Q), .sel(MUX));  // open: in7
endmodule

module testMuxThing (
  input  [15:0] in_1,
  input  [15:0] in_2,
  input  [15:0] in_3,
  input  [3:0] in_4,
  input  [15:0] in_5,
  input  [15:0] in_6,
  input  [15:0] in_7,
  output [15:0] out_8,
  output [15:0] out_9
);

  Multiplexer #(.select(4), .width(32)) multiplexer_1 (
    .in0({in_2, in_1}), .in1({in_3, in_1}), .in2({in_5, in_1}), .in3({in_6, in_1}), .in4({in_7, in_1}),
    .in5({in_3, in_2}), .in6({in_5, in_2}), .in7({in_6, in_2}), .in8({in_7, in_2}), .in9({in_5, in_3}),
    .in10({in_6, in_3}), .in11({in_7, in_3}), .in12({in_6, in_5}), .in13({in_7, in_5}), .in14({in_7, in_6}),
    .out({out_9, out_8}), .sel(in_4));  // open: in15

  // Other names for the same wires on the sheet: Ain[15:0] = in_1; Bin[15:0] = in_2; Cin[15:0] = in_3;
  //   TMPin[15:0] = in_5; MEMin[15:0] = in_6; OPin[15:0] = in_7
endmodule
